// Logisim project XF4U.circ as structural Verilog: 8 circuits, main circuit main
module main (
  input  in_1,
  input  in_2
);

  wire clock_1_out, \core_1_такт_2 , \nfu_1_выход , not_1_out, pcu_1_out_2, \Вкл_Выкл_out , \Сброс_out ;
  wire [7:0] \core_1_адрес_в_кеше , \core_1_вывод , \core_1_вывод_2 , \core_1_вывод_3 , multiplexer_1_out,
       ram_1_data, rom_1_data, undriven, undriven_2, undriven_3;

  Clock clock_1 (.out(clock_1_out));
  Button \u_Вкл_Выкл  (.out(\Вкл_Выкл_out ));
  pcu pcu_1 (.\Вкл_выкл_кнп (\Вкл_Выкл_out ), .out_2(pcu_1_out_2));
  nfu nfu_1 (.\Такт (clock_1_out), .\Вкл (pcu_1_out_2), .\Выход (\nfu_1_выход ));
  Button \u_Сброс  (.out(\Сброс_out ));
  ROM rom_1 (.addr(undriven), .data(rom_1_data));  // open: sel
  Multiplexer #(.width(8)) multiplexer_1 (
    .in0(\core_1_адрес_в_кеше ), .in1(undriven_3), .out(multiplexer_1_out), .sel(in_1));  // open: en
  core core_1 (
    .\Сброс_УИ (\Сброс_out ), .\Включен (in_2), .\Данные_из_кеша (ram_1_data),
    .\Адрес_В_Кеше (\core_1_адрес_в_кеше ), .\Вывод (\core_1_вывод ), .\Такт (\nfu_1_выход ),
    .\Вывод_2 (\core_1_вывод_2 ), .\Вывод_3 (\core_1_вывод_3 ), .\такт_2 (\core_1_такт_2 ));
  RAM #(.bus("separate")) ram_1 (
    .addr(multiplexer_1_out), .din(undriven_2), .data(ram_1_data), .str(in_1), .clk(\nfu_1_выход ),
    .ld(not_1_out));  // open: sel, clr
  not not_1 (not_1_out, in_1);
endmodule

module cu (
  input  [7:0] in_1,
  input  in_2,
  input  [7:0] \Значение_рег_2 ,
  output Rw,
  output Pcc,
  output RWC,
  output [3:0] \АЛУВ ,
  output \АЛР ,
  output \ВЫВ 
);

  wire comparator_1_eq, comparator_2_eq, comparator_3_eq, comparator_4_eq, comparator_5_eq, comparator_6_eq,
       comparator_7_eq, multiplexer_2_out, multiplexer_3_out, multiplexer_7_out;

  Comparator comparator_1 (.a({8{1'b1}}), .b(\Значение_рег_2 ), .eq(comparator_1_eq));  // open: gt, lt
  Comparator comparator_2 (.a(in_1), .b(8'h1), .eq(comparator_2_eq));  // open: gt, lt
  Comparator comparator_3 (.a(in_1), .b(8'h4), .eq(comparator_3_eq));  // open: gt, lt
  Comparator comparator_4 (.a(in_1), .b(8'h3), .eq(comparator_4_eq));  // open: gt, lt
  Comparator #(.width(4)) comparator_5 (.a(in_1[7:4]), .b(4'b0001), .eq(comparator_5_eq));  // open: gt, lt
  Comparator comparator_6 (.a(in_1), .b(8'h2), .eq(comparator_6_eq));  // open: gt, lt
  Comparator comparator_7 (.a(in_1), .b(8'h5), .eq(comparator_7_eq));  // open: gt, lt
  Multiplexer multiplexer_1 (.in0(1'b0), .in1(comparator_5_eq), .out(\АЛР ), .sel(in_2));  // open: en
  Multiplexer multiplexer_2 (.in0(1'b0), .in1(comparator_2_eq), .out(multiplexer_2_out), .sel(in_2));  // open: en
  Multiplexer multiplexer_3 (.in0(1'b0), .in1(comparator_3_eq), .out(multiplexer_3_out), .sel(in_2));  // open: en
  Multiplexer multiplexer_4 (.in0(1'b0), .in1(comparator_4_eq), .out(RWC), .sel(in_2));  // open: en
  Multiplexer #(.width(4)) multiplexer_5 (.in0(4'b0000), .in1(in_1[3:0]), .out(\АЛУВ ), .sel(\АЛР ));  // open: en
  Multiplexer multiplexer_6 (.in0(1'b0), .in1(comparator_6_eq), .out(\ВЫВ ), .sel(in_2));  // open: en
  Multiplexer multiplexer_7 (
    .in0(1'b0), .in1(comparator_1_eq), .out(multiplexer_7_out), .sel(comparator_7_eq));  // open: en
  or or_1 (Rw, multiplexer_2_out, RWC);
  Multiplexer multiplexer_8 (
    .in0(multiplexer_3_out), .in1(multiplexer_7_out), .out(Pcc), .sel(multiplexer_7_out));  // open: en
endmodule

module alu (
  input  [3:0] in_1,
  input  [7:0] \Ч1 ,
  input  [7:0] \Ч2 ,
  output [7:0] out_4
);

  wire [7:0] adder_1_out, demultiplexer_1_out1, demultiplexer_1_out2, demultiplexer_1_out3,
       demultiplexer_1_out4, demultiplexer_2_out1, demultiplexer_2_out2, demultiplexer_2_out3,
       demultiplexer_2_out4, divider_1_out, multiplier_1_out, subtractor_1_out;

  Demultiplexer #(.select(4), .width(8)) demultiplexer_1 (
    .out1(demultiplexer_1_out1), .out2(demultiplexer_1_out2), .out3(demultiplexer_1_out3),
    .out4(demultiplexer_1_out4), .in(\Ч1 ), .sel(in_1));  // open: out0, out5, out6, out7, out8, out9, out10, out11, out12, out13, out14, out15, en
  Demultiplexer #(.select(4), .width(8)) demultiplexer_2 (
    .out1(demultiplexer_2_out1), .out2(demultiplexer_2_out2), .out3(demultiplexer_2_out3),
    .out4(demultiplexer_2_out4), .in(\Ч2 ), .sel(in_1));  // open: out0, out5, out6, out7, out8, out9, out10, out11, out12, out13, out14, out15, en
  Adder adder_1 (.a(demultiplexer_1_out1), .b(demultiplexer_2_out1), .out(adder_1_out));  // open: cin, cout
  Subtractor subtractor_1 (
    .a(demultiplexer_1_out2), .b(demultiplexer_2_out2), .out(subtractor_1_out));  // open: bin, bout
  Multiplier multiplier_1 (
    .a(demultiplexer_1_out3), .b(demultiplexer_2_out3), .out(multiplier_1_out));  // open: cin, cout
  Divider divider_1 (.a(demultiplexer_1_out4), .b(demultiplexer_2_out4), .out(divider_1_out));  // open: upper, rem
  Multiplexer #(.select(4), .width(8)) multiplexer_1 (
    .in0({8{1'b0}}), .in1(adder_1_out), .in2(subtractor_1_out), .in3(multiplier_1_out), .in4(divider_1_out),
    .out(out_4), .sel(in_1));  // open: in5, in6, in7, in8, in9, in10, in11, in12, in13, in14, in15, en
endmodule

module \reg  (
  input  [7:0] a1,
  input  [7:0] a2,
  input  [7:0] aw,
  input  [7:0] dw,
  input  Rw,
  output [7:0] d1,
  output [7:0] d2
);

  wire [2:0] bit_extender_1_out, bit_extender_2_out, bit_extender_3_out;
  wire [7:0] demultiplexer_1_out0, demultiplexer_1_out1, demultiplexer_1_out2, demultiplexer_1_out3,
       demultiplexer_1_out4, demultiplexer_1_out5, demultiplexer_1_out6, demultiplexer_1_out7, register_1_q,
       register_2_q, register_3_q, register_4_q, register_5_q, register_6_q, register_7_q, register_8_q;

  Bit_Extender #(.out_width(3)) bit_extender_1 (.in(a1), .out(bit_extender_1_out));
  Bit_Extender #(.out_width(3)) bit_extender_2 (.in(a2), .out(bit_extender_2_out));
  Demultiplexer #(.select(3), .width(8)) demultiplexer_1 (
    .out0(demultiplexer_1_out0), .out1(demultiplexer_1_out1), .out2(demultiplexer_1_out2),
    .out3(demultiplexer_1_out3), .out4(demultiplexer_1_out4), .out5(demultiplexer_1_out5),
    .out6(demultiplexer_1_out6), .out7(demultiplexer_1_out7), .in(dw), .sel(bit_extender_3_out));  // open: en
  Bit_Extender #(.out_width(3)) bit_extender_3 (.in(aw), .out(bit_extender_3_out));
  Register register_1 (.D(demultiplexer_1_out0), .Q(register_1_q), .clk(Rw));  // open: en, clr
  Register register_2 (.D(demultiplexer_1_out4), .Q(register_2_q), .clk(Rw));  // open: en, clr
  Register register_3 (.D(demultiplexer_1_out1), .Q(register_3_q), .clk(Rw));  // open: en, clr
  Register register_4 (.D(demultiplexer_1_out5), .Q(register_4_q), .clk(Rw));  // open: en, clr
  Register register_5 (.D(demultiplexer_1_out2), .Q(register_5_q), .clk(Rw));  // open: en, clr
  Register register_6 (.D(demultiplexer_1_out6), .Q(register_6_q), .clk(Rw));  // open: en, clr
  Register register_7 (.D(demultiplexer_1_out3), .Q(register_7_q), .clk(Rw));  // open: en, clr
  Register register_8 (.D(demultiplexer_1_out7), .Q(register_8_q), .clk(Rw));  // open: en, clr
  Multiplexer #(.select(3), .width(8)) multiplexer_1 (
    .in0(register_1_q), .in1(register_3_q), .in2(register_5_q), .in3(register_7_q), .in4(register_2_q),
    .in5(register_4_q), .in6(register_6_q), .in7(register_8_q), .out(d1), .sel(bit_extender_1_out));  // open: en
  Multiplexer #(.select(3), .width(8)) multiplexer_2 (
    .in0(register_1_q), .in1(register_3_q), .in2(register_5_q), .in3(register_7_q), .in4(register_2_q),
    .in5(register_4_q), .in6(register_6_q), .in7(register_8_q), .out(d2), .sel(bit_extender_2_out));  // open: en
endmodule

module core (
  input  \Сброс_УИ ,
  input  \Такт ,
  input  \Включен ,
  input  [7:0] \Данные_из_кеша ,
  output [7:0] \Адрес_В_Кеше ,
  output [7:0] \Вывод ,
  output [7:0] \Вывод_2 ,
  output [7:0] \Вывод_3 ,
  output \такт_2 
);

  wire counter_2_carry, cu_1_pcc, cu_1_rw, cu_1_rwc, \cu_1_алр , \cu_1_выв , demultiplexer_2_out0,
       demultiplexer_2_out1, demultiplexer_2_out2, multiplexer_1_out;
  wire [1:0] counter_2_q;
  wire [3:0] \cu_1_алув ;
  wire [7:0] adder_1_out, alu_1_out_4, demultiplexer_1_out0, demultiplexer_1_out1, demultiplexer_1_out2,
       multiplexer_2_out, multiplexer_3_out, reg_1_d1, reg_1_d2, register_1_q, register_2_q, register_3_q,
       register_7_q;

  Multiplexer multiplexer_1 (.in0(1'b0), .in1(\Такт ), .out(multiplexer_1_out), .sel(\Включен ));  // open: en
  Multiplexer #(.width(8)) multiplexer_2 (
    .in0(adder_1_out), .in1(reg_1_d1), .out(multiplexer_2_out), .sel(cu_1_pcc));  // open: en
  Counter counter_1 (
    .D(multiplexer_2_out), .Q(\Адрес_В_Кеше ), .clk(multiplexer_1_out), .clr(\Сброс_УИ ));  // open: load, count, carry
  Adder adder_1 (.a(\Адрес_В_Кеше ), .b(8'h1), .out(adder_1_out));  // open: cin, cout
  Counter #(.width(2), .max('h3)) counter_2 (
    .Q(counter_2_q), .carry(counter_2_carry), .clk(multiplexer_1_out), .clr(\Сброс_УИ ));  // open: load, D, count
  Demultiplexer #(.select(2), .width(8)) demultiplexer_1 (
    .out0(demultiplexer_1_out0), .out1(demultiplexer_1_out1), .out2(demultiplexer_1_out2),
    .in(\Данные_из_кеша ), .sel(counter_2_q));  // open: out3, en
  Demultiplexer #(.select(2)) demultiplexer_2 (
    .out0(demultiplexer_2_out0), .out1(demultiplexer_2_out1), .out2(demultiplexer_2_out2),
    .in(multiplexer_1_out), .sel(counter_2_q));  // open: out3, en
  Register register_1 (.D(demultiplexer_1_out0), .Q(register_1_q), .clk(demultiplexer_2_out0));  // open: en, clr
  Register register_2 (.D(demultiplexer_1_out1), .Q(register_2_q), .clk(demultiplexer_2_out1));  // open: en, clr
  Register register_3 (.D(demultiplexer_1_out2), .Q(register_3_q), .clk(demultiplexer_2_out2));  // open: en, clr
  Multiplexer #(.width(8)) multiplexer_3 (
    .in0(register_3_q), .in1(register_7_q), .out(multiplexer_3_out), .sel(cu_1_rwc));  // open: en
  cu cu_1 (
    .in_1(register_1_q), .Rw(cu_1_rw), .in_2(counter_2_carry), .Pcc(cu_1_pcc), .RWC(cu_1_rwc),
    .\АЛУВ (\cu_1_алув ), .\АЛР (\cu_1_алр ), .\ВЫВ (\cu_1_выв ), .\Значение_рег_2 (reg_1_d2));
  \reg  reg_1 (
    .Rw(cu_1_rw), .a2(register_3_q), .a1(register_2_q), .aw(register_2_q), .dw(multiplexer_3_out),
    .d1(reg_1_d1), .d2(reg_1_d2));
  Register register_4 (.D(reg_1_d1), .Q(\Вывод ), .clk(\cu_1_выв ));  // open: en, clr
  Register register_5 (.Q(\Вывод_2 ));  // open: D, en, clk, clr
  Register register_6 (.Q(\Вывод_3 ));  // open: D, en, clk, clr
  alu alu_1 (.in_1(\cu_1_алув ), .\Ч1 (reg_1_d1), .\Ч2 (reg_1_d2), .out_4(alu_1_out_4));
  Register register_7 (.D(alu_1_out_4), .Q(register_7_q), .clk(\cu_1_алр ));  // open: en, clr

  assign \такт_2  = 1'b1;
endmodule

module ccu (
  input  \Сброс ,
  input  \Такт ,
  input  [7:0] \Данные ,
  output [7:0] \Адресс ,
  output [7:0] \Адресс_ядра_1 ,
  output [7:0] \Адресс_ядра_2 ,
  output [7:0] \Данные_ядра_1 ,
  output [7:0] \Данные_ядра_2 
);

  wire demultiplexer_1_out0, demultiplexer_1_out1, register_1_q;

  Counter counter_1 (.Q(\Адресс ), .clk(\Такт ), .clr(\Сброс ));  // open: load, D, count, carry
  Register #(.width(1)) register_1 (.Q(register_1_q), .clr(\Сброс ));  // open: D, en, clk
  Demultiplexer demultiplexer_1 (
    .out0(demultiplexer_1_out0), .out1(demultiplexer_1_out1), .in(\Такт ), .sel(register_1_q));  // open: en
  Demultiplexer #(.width(8)) demultiplexer_2 (
    .out0(\Данные_ядра_1 ), .out1(\Данные_ядра_2 ), .in(\Данные ), .sel(register_1_q));  // open: en
  Counter counter_2 (.Q(\Адресс_ядра_1 ), .clk(demultiplexer_1_out0), .clr(\Сброс ));  // open: load, D, count, carry
  Counter counter_3 (.Q(\Адресс_ядра_2 ), .clk(demultiplexer_1_out1), .clr(\Сброс ));  // open: load, D, count, carry
endmodule

module pcu (
  input  \Вкл_выкл_кнп ,
  output out_2
);

  Counter #(.width(1), .max('h1)) counter_1 (.Q(out_2), .clk(\Вкл_выкл_кнп ));  // open: load, D, count, carry, clr
endmodule

module nfu (
  input  \Такт ,
  input  \Вкл ,
  output \Выход 
);

  wire not_1_out;

  assign \Выход  = not_1_out ? \Вкл  : 1'bz;  // Controlled_Buffer controlled_buffer_1
  assign \Выход  = \Вкл  ? \Такт  : 1'bz;  // Controlled_Buffer controlled_buffer_2
  not not_1 (not_1_out, \Вкл );
endmodule
