// Logisim project tvc.circ as structural Verilog: 1 circuit, main circuit main
module main (
  input  [7:0] in_1,
  output [6:0] out_2,
  output reset
);

  Comparator comparator_1 (.a(in_1), .b({8{1'b1}}), .eq(reset));  // open: gt, lt

  assign out_2 = in_1[6:0];
endmodule
