// Logisim project П-1УМ.circ as structural Verilog: 11 circuits, main circuit main
module main (
);

  wire \ccu_1_включение_ядра , \ccu_1_запись___чтение_кеша , clock_1_out,
       \core_1_разрешить_выводить_в_консоль , \core_1_такт_2 , \nfu_1_выход , not_1_out, not_2_out,
       pcu_1_out_2, \rtr_1_выполнено , tvc_1_out_5, tvc_1_out_6, undriven, undriven_2, undriven_3,
       \Вкл_Выкл_out , \Сброс_out ;
  wire [3:0] \core_1_вывод_в_консоль , \core_1_вывод_в_консоль_2 , \core_2_вывод_в_консоль ,
       \core_2_вывод_в_консоль_2 ;
  wire [6:0] tvc_1_out_4;
  wire [7:0] \core_1_адрес , \core_1_адрес_в_кеше , \core_1_вывод_адрес_для_пзу ,
       \core_1_вывод_адрес_для_пзу_конец , \core_1_данные_2 , \core_2_адрес , \core_2_адрес_в_кеше ,
       \core_2_данные_2 , \mkz_1_ядро_1 , \mkz_1_ядро_2 , multiplexer_1_out, multiplexer_2_out, ram_1_data,
       ram_2_data, rom_1_data, \rtr_1_адрес , \rtr_1_адрес_пзу ;

  Button \u_Сброс  (.out(\Сброс_out ));
  Clock clock_1 (.out(clock_1_out));
  Button \u_Вкл_Выкл  (.out(\Вкл_Выкл_out ));
  pcu pcu_1 (.\Вкл_выкл_кнп (\Вкл_Выкл_out ), .out_2(pcu_1_out_2));
  ROM rom_1 (.addr(\rtr_1_адрес_пзу ), .data(rom_1_data));  // open: sel
  nfu nfu_1 (.\Такт (clock_1_out), .\Вкл (pcu_1_out_2), .\Выход (\nfu_1_выход ));
  core core_1 (
    .\Сброс_УИ (\Сброс_out ), .\Включен (\ccu_1_запись___чтение_кеша ), .\Данные_из_кеша (ram_2_data),
    .\Адрес_В_Кеше (\core_1_адрес_в_кеше ), .\Вывод_адрес_для_пзу (\core_1_вывод_адрес_для_пзу ),
    .\Такт (\nfu_1_выход ), .\Вывод_адрес_для_пзу_конец (\core_1_вывод_адрес_для_пзу_конец ),
    .\такт_2 (\core_1_такт_2 ), .\Вывод_в_консоль ({\core_1_вывод_в_консоль_2 , \core_1_вывод_в_консоль }),
    .\разрешить_выводить_в_консоль (\core_1_разрешить_выводить_в_консоль ), .\Адрес (\core_1_адрес ),
    .\Данные_2 (\core_1_данные_2 ), .\Данные (\mkz_1_ядро_1 ), .\Запись (undriven));
  Multiplexer #(.width(8)) multiplexer_1 (
    .in0(\core_2_адрес_в_кеше ), .in1(\rtr_1_адрес ), .out(multiplexer_1_out), .sel(undriven_3));  // open: en
  Multiplexer #(.width(8)) multiplexer_2 (
    .in0(\core_1_адрес_в_кеше ), .in1(\rtr_1_адрес ), .out(multiplexer_2_out), .sel(\ccu_1_включение_ядра ));  // open: en
  MKZ mkz_1 (
    .\Адрес (\core_1_адрес ), .\Данные (\core_1_данные_2 ), .\Адрес_2 (\core_2_адрес ),
    .\Данные_2 (\core_2_данные_2 ), .\Ядро_1 (\mkz_1_ядро_1 ), .\Ядро_2 (\mkz_1_ядро_2 ));
  core core_2 (
    .\Сброс_УИ (\Сброс_out ), .\Включен (\ccu_1_запись___чтение_кеша ), .\Данные_из_кеша (ram_1_data),
    .\Адрес_В_Кеше (\core_2_адрес_в_кеше ), .\Такт (\nfu_1_выход ),
    .\Вывод_в_консоль ({\core_2_вывод_в_консоль_2 , \core_2_вывод_в_консоль }), .\Адрес (\core_2_адрес ),
    .\Данные_2 (\core_2_данные_2 ), .\Данные (\mkz_1_ядро_2 ), .\Запись (undriven_2));  // open: Вывод_адрес_для_пзу, Вывод_адрес_для_пзу_конец, такт_2, разрешить_выводить_в_консоль
  RtR rtr_1 (
    .\Такт (\nfu_1_выход ), .\Сброс (\Сброс_out ), .\Адрес_для_пзу (\core_1_вывод_адрес_для_пзу ),
    .\Загрузка_адреса_для_пзу (\core_1_такт_2 ), .\Адрес_для_пзу_конец (\core_1_вывод_адрес_для_пзу_конец ),
    .\Адрес (\rtr_1_адрес ), .\Адрес_ПЗУ (\rtr_1_адрес_пзу ), .\Выполнено (\rtr_1_выполнено ));
  RAM #(.bus("separate")) ram_1 (
    .addr(multiplexer_1_out), .din(rom_1_data), .data(ram_1_data), .str(undriven_3), .clk(\nfu_1_выход ),
    .ld(not_1_out));  // open: sel, clr
  not not_1 (not_1_out, undriven_3);
  RAM #(.bus("separate")) ram_2 (
    .addr(multiplexer_2_out), .din(rom_1_data), .data(ram_2_data), .str(\ccu_1_включение_ядра ),
    .clk(\nfu_1_выход ), .ld(not_2_out));  // open: sel, clr
  not not_2 (not_2_out, \ccu_1_включение_ядра );
  CCU ccu_1 (
    .\Вход_РтР (\rtr_1_выполнено ), .\Запрос_на_загрузку (\core_1_такт_2 ),
    .\Включение_ядра (\ccu_1_включение_ядра ), .\Запись___чтение_кеша (\ccu_1_запись___чтение_кеша ));
  tvc tvc_1 (
    .in_1({\core_1_вывод_в_консоль_2 , \core_1_вывод_в_консоль }), .in_2(\nfu_1_выход ),
    .in_3(\core_1_разрешить_выводить_в_консоль ), .out_4(tvc_1_out_4), .out_5(tvc_1_out_5),
    .out_6(tvc_1_out_6));
  TTY tty_1 (.data(tvc_1_out_4), .clk(tvc_1_out_5), .clr(tvc_1_out_6));  // open: we
  Hex_Digit_Display hex_digit_display_1 (.value(\core_1_вывод_в_консоль ));  // open: dp
  Hex_Digit_Display hex_digit_display_2 (.value(\core_1_вывод_в_консоль_2 ));  // open: dp
  Hex_Digit_Display hex_digit_display_3 (.value(\core_2_вывод_в_консоль_2 ));  // open: dp
  Hex_Digit_Display hex_digit_display_4 (.value(\core_2_вывод_в_консоль ));  // open: dp
endmodule

module cu (
  input  [7:0] \команда ,
  input  \Включение ,
  input  [7:0] \Значение_рег_2 ,
  output Rw,
  output Pcc,
  output RWC,
  output [3:0] \АЛУ_команда ,
  output \АЛР ,
  output \ВЫВОД ,
  output LD,
  output \ПД ,
  output \ЗД 
);

  wire comparator_1_eq, comparator_2_eq, comparator_3_eq, comparator_4_eq, comparator_5_eq, comparator_6_eq,
       comparator_7_eq, comparator_8_eq, comparator_9_eq, comparator_10_eq, multiplexer_2_out,
       multiplexer_3_out, multiplexer_7_out;

  Comparator comparator_1 (.a({8{1'b1}}), .b(\Значение_рег_2 ), .eq(comparator_1_eq));  // open: gt, lt
  Comparator #(.width(4)) comparator_2 (.a(\команда [7:4]), .b(4'b1111), .eq(comparator_2_eq));  // open: gt, lt
  Comparator comparator_3 (.a(\команда ), .b(8'h1), .eq(comparator_3_eq));  // open: gt, lt
  Comparator comparator_4 (.a(\команда ), .b(8'h4), .eq(comparator_4_eq));  // open: gt, lt
  Comparator comparator_5 (.a(\команда ), .b(8'h3), .eq(comparator_5_eq));  // open: gt, lt
  Comparator #(.width(4)) comparator_6 (.a(\команда [7:4]), .b(4'b0001), .eq(comparator_6_eq));  // open: gt, lt
  Comparator comparator_7 (.a(\команда ), .b(8'h2), .eq(comparator_7_eq));  // open: gt, lt
  Comparator comparator_8 (.a(\команда ), .b(8'h5), .eq(comparator_8_eq));  // open: gt, lt
  Comparator comparator_9 (.a(\команда ), .b(8'h6), .eq(comparator_9_eq));  // open: gt, lt
  Comparator comparator_10 (.a(\команда ), .b(8'h7), .eq(comparator_10_eq));  // open: gt, lt
  Multiplexer multiplexer_1 (.in0(1'b0), .in1(comparator_6_eq), .out(\АЛР ), .sel(\Включение ));  // open: en
  Multiplexer multiplexer_2 (
    .in0(1'b0), .in1(comparator_3_eq), .out(multiplexer_2_out), .sel(\Включение ));  // open: en
  Multiplexer multiplexer_3 (
    .in0(1'b0), .in1(comparator_4_eq), .out(multiplexer_3_out), .sel(\Включение ));  // open: en
  Multiplexer multiplexer_4 (.in0(1'b0), .in1(comparator_5_eq), .out(RWC), .sel(\Включение ));  // open: en
  Multiplexer #(.width(4)) multiplexer_5 (
    .in0(4'b0000), .in1(\команда [3:0]), .out(\АЛУ_команда ), .sel(\АЛР ));  // open: en
  Multiplexer multiplexer_6 (.in0(1'b0), .in1(comparator_7_eq), .out(\ВЫВОД ), .sel(\Включение ));  // open: en
  Multiplexer multiplexer_7 (
    .in0(1'b0), .in1(comparator_1_eq), .out(multiplexer_7_out), .sel(comparator_8_eq));  // open: en
  Multiplexer multiplexer_8 (.in0(1'b0), .in1(comparator_2_eq), .out(LD), .sel(comparator_2_eq));  // open: en
  Multiplexer multiplexer_9 (.in0(1'b0), .in1(comparator_9_eq), .out(\ПД ), .sel(comparator_9_eq));  // open: en
  Multiplexer multiplexer_10 (.in0(1'b0), .in1(comparator_10_eq), .out(\ЗД ), .sel(comparator_10_eq));  // open: en
  or or_1 (Rw, multiplexer_2_out, RWC);
  Multiplexer multiplexer_11 (
    .in0(multiplexer_3_out), .in1(multiplexer_7_out), .out(Pcc), .sel(multiplexer_7_out));  // open: en
endmodule

module alu (
  input  [3:0] in_1,
  input  [7:0] \Ч1 ,
  input  [7:0] \Ч2 ,
  output [7:0] out_4
);

  wire [7:0] adder_1_out, demultiplexer_1_out1, demultiplexer_1_out2, demultiplexer_1_out3,
       demultiplexer_1_out4, demultiplexer_2_out1, demultiplexer_2_out2, demultiplexer_2_out3,
       demultiplexer_2_out4, divider_1_out, multiplier_1_out, subtractor_1_out;

  Demultiplexer #(.select(4), .width(8)) demultiplexer_1 (
    .out1(demultiplexer_1_out1), .out2(demultiplexer_1_out2), .out3(demultiplexer_1_out3),
    .out4(demultiplexer_1_out4), .in(\Ч1 ), .sel(in_1));  // open: out0, out5, out6, out7, out8, out9, out10, out11, out12, out13, out14, out15, en
  Demultiplexer #(.select(4), .width(8)) demultiplexer_2 (
    .out1(demultiplexer_2_out1), .out2(demultiplexer_2_out2), .out3(demultiplexer_2_out3),
    .out4(demultiplexer_2_out4), .in(\Ч2 ), .sel(in_1));  // open: out0, out5, out6, out7, out8, out9, out10, out11, out12, out13, out14, out15, en
  Adder adder_1 (.a(demultiplexer_1_out1), .b(demultiplexer_2_out1), .out(adder_1_out));  // open: cin, cout
  Subtractor subtractor_1 (
    .a(demultiplexer_1_out2), .b(demultiplexer_2_out2), .out(subtractor_1_out));  // open: bin, bout
  Multiplier multiplier_1 (
    .a(demultiplexer_1_out3), .b(demultiplexer_2_out3), .out(multiplier_1_out));  // open: cin, cout
  Divider divider_1 (.a(demultiplexer_1_out4), .b(demultiplexer_2_out4), .out(divider_1_out));  // open: upper, rem
  Multiplexer #(.select(4), .width(8)) multiplexer_1 (
    .in0({8{1'b0}}), .in1(adder_1_out), .in2(subtractor_1_out), .in3(multiplier_1_out), .in4(divider_1_out),
    .out(out_4), .sel(in_1));  // open: in5, in6, in7, in8, in9, in10, in11, in12, in13, in14, in15, en
endmodule

module \reg  (
  input  [7:0] a1,
  input  [7:0] a2,
  input  [7:0] aw,
  input  [7:0] dw,
  input  Rw,
  output [7:0] d1,
  output [7:0] d2
);

  wire demultiplexer_2_out0, demultiplexer_2_out1, demultiplexer_2_out2, demultiplexer_2_out3,
       demultiplexer_2_out4, demultiplexer_2_out5, demultiplexer_2_out6, demultiplexer_2_out7;
  wire [2:0] bit_extender_1_out, bit_extender_2_out, bit_extender_3_out;
  wire [7:0] demultiplexer_1_out0, demultiplexer_1_out1, demultiplexer_1_out2, demultiplexer_1_out3,
       demultiplexer_1_out4, demultiplexer_1_out5, demultiplexer_1_out6, demultiplexer_1_out7, register_1_q,
       register_2_q, register_3_q, register_4_q, register_5_q, register_6_q, register_7_q, register_8_q;

  Bit_Extender #(.out_width(3)) bit_extender_1 (.in(a1), .out(bit_extender_1_out));
  Bit_Extender #(.out_width(3)) bit_extender_2 (.in(a2), .out(bit_extender_2_out));
  Demultiplexer #(.select(3), .width(8)) demultiplexer_1 (
    .out0(demultiplexer_1_out0), .out1(demultiplexer_1_out1), .out2(demultiplexer_1_out2),
    .out3(demultiplexer_1_out3), .out4(demultiplexer_1_out4), .out5(demultiplexer_1_out5),
    .out6(demultiplexer_1_out6), .out7(demultiplexer_1_out7), .in(dw), .sel(bit_extender_3_out));  // open: en
  Bit_Extender #(.out_width(3)) bit_extender_3 (.in(aw), .out(bit_extender_3_out));
  Demultiplexer #(.select(3)) demultiplexer_2 (
    .out0(demultiplexer_2_out0), .out1(demultiplexer_2_out1), .out2(demultiplexer_2_out2),
    .out3(demultiplexer_2_out3), .out4(demultiplexer_2_out4), .out5(demultiplexer_2_out5),
    .out6(demultiplexer_2_out6), .out7(demultiplexer_2_out7), .in(Rw), .sel(bit_extender_3_out));  // open: en
  Register register_1 (.D(demultiplexer_1_out0), .Q(register_1_q), .clk(demultiplexer_2_out0));  // open: en, clr
  Register register_2 (.D(demultiplexer_1_out4), .Q(register_2_q), .clk(demultiplexer_2_out4));  // open: en, clr
  Register register_3 (.D(demultiplexer_1_out1), .Q(register_3_q), .clk(demultiplexer_2_out1));  // open: en, clr
  Register register_4 (.D(demultiplexer_1_out5), .Q(register_4_q), .clk(demultiplexer_2_out5));  // open: en, clr
  Register register_5 (.D(demultiplexer_1_out2), .Q(register_5_q), .clk(demultiplexer_2_out2));  // open: en, clr
  Register register_6 (.D(demultiplexer_1_out6), .Q(register_6_q), .clk(demultiplexer_2_out6));  // open: en, clr
  Register register_7 (.D(demultiplexer_1_out3), .Q(register_7_q), .clk(demultiplexer_2_out3));  // open: en, clr
  Register register_8 (.D(demultiplexer_1_out7), .Q(register_8_q), .clk(demultiplexer_2_out7));  // open: en, clr
  Multiplexer #(.select(3), .width(8)) multiplexer_1 (
    .in0(register_1_q), .in1(register_3_q), .in2(register_5_q), .in3(register_7_q), .in4(register_2_q),
    .in5(register_4_q), .in6(register_6_q), .in7(register_8_q), .out(d1), .sel(bit_extender_1_out));  // open: en
  Multiplexer #(.select(3), .width(8)) multiplexer_2 (
    .in0(register_1_q), .in1(register_3_q), .in2(register_5_q), .in3(register_7_q), .in4(register_2_q),
    .in5(register_4_q), .in6(register_6_q), .in7(register_8_q), .out(d2), .sel(bit_extender_2_out));  // open: en
endmodule

module core (
  input  \Сброс_УИ ,
  input  \Такт ,
  input  \Включен ,
  input  [7:0] \Данные_из_кеша ,
  input  [7:0] \Данные ,
  input  \Запись ,
  output [7:0] \Адрес_В_Кеше ,
  output [7:0] \Вывод_адрес_для_пзу ,
  output [7:0] \Вывод_адрес_для_пзу_конец ,
  output \такт_2 ,
  output [7:0] \Вывод_в_консоль ,
  output \разрешить_выводить_в_консоль ,
  output [7:0] \Адрес ,
  output [7:0] \Данные_2 
);

  wire counter_2_carry, cu_1_pcc, cu_1_rw, cu_1_rwc, \cu_1_алр , \cu_1_зд , \cu_1_пд , demultiplexer_2_out0,
       demultiplexer_2_out1, demultiplexer_2_out2, multiplexer_1_out;
  wire [1:0] counter_2_q;
  wire [3:0] \cu_1_алу_команда ;
  wire [7:0] adder_1_out, alu_1_out_4, demultiplexer_1_out0, demultiplexer_1_out1, demultiplexer_1_out2,
       multiplexer_2_out, multiplexer_3_out, multiplexer_4_out, reg_1_d1, reg_1_d2, register_1_q,
       register_2_q, register_3_q, register_4_q, register_8_q;

  Multiplexer multiplexer_1 (.in0(1'b0), .in1(\Такт ), .out(multiplexer_1_out), .sel(\Включен ));  // open: en
  Multiplexer #(.width(8)) multiplexer_2 (
    .in0(adder_1_out), .in1(reg_1_d1), .out(multiplexer_2_out), .sel(cu_1_pcc));  // open: en
  Counter counter_1 (
    .D(multiplexer_2_out), .Q(\Адрес_В_Кеше ), .clk(multiplexer_1_out), .clr(\Сброс_УИ ));  // open: load, count, carry
  Adder adder_1 (.a(\Адрес_В_Кеше ), .b(8'h1), .out(adder_1_out));  // open: cin, cout
  Register register_1 (.D(\Данные ), .Q(register_1_q), .clk(\Запись ));  // open: en, clr
  Counter #(.width(2), .max('h3)) counter_2 (
    .Q(counter_2_q), .carry(counter_2_carry), .clk(multiplexer_1_out), .clr(\Сброс_УИ ));  // open: load, D, count
  Demultiplexer #(.select(2), .width(8)) demultiplexer_1 (
    .out0(demultiplexer_1_out0), .out1(demultiplexer_1_out1), .out2(demultiplexer_1_out2),
    .in(\Данные_из_кеша ), .sel(counter_2_q));  // open: out3, en
  Demultiplexer #(.select(2)) demultiplexer_2 (
    .out0(demultiplexer_2_out0), .out1(demultiplexer_2_out1), .out2(demultiplexer_2_out2),
    .in(multiplexer_1_out), .sel(counter_2_q));  // open: out3, en
  Register register_2 (.D(demultiplexer_1_out0), .Q(register_2_q), .clk(demultiplexer_2_out0));  // open: en, clr
  Register register_3 (.D(demultiplexer_1_out1), .Q(register_3_q), .clk(demultiplexer_2_out1));  // open: en, clr
  Register register_4 (.D(demultiplexer_1_out2), .Q(register_4_q), .clk(demultiplexer_2_out2));  // open: en, clr
  Multiplexer #(.width(8)) multiplexer_3 (
    .in0(register_8_q), .in1(register_1_q), .out(multiplexer_3_out), .sel(\cu_1_пд ));  // open: en
  Multiplexer #(.width(8)) multiplexer_4 (
    .in0(register_4_q), .in1(multiplexer_3_out), .out(multiplexer_4_out), .sel(cu_1_rwc));  // open: en
  cu cu_1 (
    .\команда (register_2_q), .Rw(cu_1_rw), .\Включение (counter_2_carry), .Pcc(cu_1_pcc), .RWC(cu_1_rwc),
    .\АЛУ_команда (\cu_1_алу_команда ), .\АЛР (\cu_1_алр ), .\ВЫВОД (\разрешить_выводить_в_консоль ),
    .\Значение_рег_2 (reg_1_d2), .LD(\такт_2 ), .\ПД (\cu_1_пд ), .\ЗД (\cu_1_зд ));
  \reg  reg_1 (
    .Rw(cu_1_rw), .a2(register_4_q), .a1(register_3_q), .aw(register_3_q), .dw(multiplexer_4_out),
    .d1(reg_1_d1), .d2(reg_1_d2));
  Register register_5 (.D(reg_1_d1), .Q(\Вывод_адрес_для_пзу ), .clk(\такт_2 ));  // open: en, clr
  Register register_6 (.D(reg_1_d2), .Q(\Вывод_адрес_для_пзу_конец ), .clk(\такт_2 ));  // open: en, clr
  Register register_7 (.D(reg_1_d1), .Q(\Вывод_в_консоль ), .clk(\разрешить_выводить_в_консоль ));  // open: en, clr
  Multiplexer #(.width(8)) multiplexer_5 (.in0({8{1'b0}}), .in1(reg_1_d1), .out(\Адрес ), .sel(\cu_1_зд ));  // open: en
  Multiplexer #(.width(8)) multiplexer_6 (
    .in0({8{1'b0}}), .in1(reg_1_d2), .out(\Данные_2 ), .sel(\cu_1_зд ));  // open: en
  alu alu_1 (.in_1(\cu_1_алу_команда ), .\Ч1 (reg_1_d1), .\Ч2 (reg_1_d2), .out_4(alu_1_out_4));
  Register register_8 (.D(alu_1_out_4), .Q(register_8_q), .clk(\cu_1_алр ));  // open: en, clr
endmodule

module pcu (
  input  \Вкл_выкл_кнп ,
  output out_2
);

  Counter #(.width(1), .max('h1)) counter_1 (.Q(out_2), .clk(\Вкл_выкл_кнп ));  // open: load, D, count, carry, clr
endmodule

module nfu (
  input  \Такт ,
  input  \Вкл ,
  output \Выход 
);

  wire not_1_out;

  assign \Выход  = not_1_out ? \Вкл  : 1'bz;  // Controlled_Buffer controlled_buffer_1
  assign \Выход  = \Вкл  ? \Такт  : 1'bz;  // Controlled_Buffer controlled_buffer_2
  not not_1 (not_1_out, \Вкл );
endmodule

module RtR (
  input  \Такт ,
  input  \Сброс ,
  input  [7:0] \Адрес_для_пзу ,
  input  \Загрузка_адреса_для_пзу ,
  input  [7:0] \Адрес_для_пзу_конец ,
  output [7:0] \Адрес ,
  output [7:0] \Адрес_ПЗУ ,
  output \Выполнено 
);

  wire buffer_1_out, or_1_out, or_2_out;

  buf buffer_1 (buffer_1_out, \Загрузка_адреса_для_пзу );
  or or_1 (or_1_out, \Сброс , \Выполнено );
  or or_2 (or_2_out, buffer_1_out, \Такт );
  Counter counter_1 (.Q(\Адрес ), .clk(\Такт ), .clr(\Сброс ));  // open: load, D, count, carry
  Counter counter_2 (.D(\Адрес_для_пзу ), .Q(\Адрес_ПЗУ ), .clk(or_2_out), .clr(or_1_out));  // open: load, count, carry
  Comparator comparator_1 (.a(\Адрес_ПЗУ ), .b(\Адрес_для_пзу_конец ), .eq(\Выполнено ));  // open: gt, lt
endmodule

module CCU (
  input  \Вход_РтР ,
  input  \Запрос_на_загрузку ,
  output \Включение_ядра ,
  output \Запись___чтение_кеша 
);

  Register #(.width(1)) register_1 (
    .D(\Вход_РтР ), .Q(\Включение_ядра ), .clk(\Вход_РтР ), .clr(\Запрос_на_загрузку ));  // open: en
  not not_1 (\Запись___чтение_кеша , \Включение_ядра );
endmodule

module tvc (
  input  [7:0] in_1,
  input  in_2,
  input  in_3,
  output [6:0] out_4,
  output out_5,
  output out_6
);

  wire [6:0] multiplexer_1_out;

  Comparator comparator_1 (.a(in_1), .b({8{1'b1}}), .eq(out_6));  // open: gt, lt
  Multiplexer #(.width(7)) multiplexer_1 (
    .in0(in_1[6:0]), .in1({7{1'b0}}), .out(multiplexer_1_out), .sel(out_6));  // open: en
  Multiplexer #(.width(7)) multiplexer_2 (
    .in0({7{1'b0}}), .in1(multiplexer_1_out), .out(out_4), .sel(in_2));  // open: en

  assign out_5 = in_3;
endmodule

module MKZ (
  input  [7:0] \Адрес ,
  input  [7:0] \Данные ,
  input  [7:0] \Адрес_2 ,
  input  [7:0] \Данные_2 ,
  output [7:0] \Ядро_1 ,
  output [7:0] \Ядро_2 
);

  wire [1:0] bit_extender_1_out, bit_extender_2_out;
  wire [7:0] demultiplexer_1_out0, demultiplexer_1_out1, demultiplexer_2_out0, demultiplexer_2_out1;

  Bit_Extender #(.out_width(2)) bit_extender_1 (.in(\Адрес_2 ), .out(bit_extender_1_out));
  Bit_Extender #(.out_width(2)) bit_extender_2 (.in(\Адрес ), .out(bit_extender_2_out));
  Demultiplexer #(.select(2), .width(8)) demultiplexer_1 (
    .out0(demultiplexer_1_out0), .out1(demultiplexer_1_out1), .in(\Данные ), .sel(bit_extender_2_out));  // open: out2, out3, en
  Demultiplexer #(.select(2), .width(8)) demultiplexer_2 (
    .out0(demultiplexer_2_out0), .out1(demultiplexer_2_out1), .in(\Данные_2 ), .sel(bit_extender_1_out));  // open: out2, out3, en
  assign \Ядро_2  = demultiplexer_1_out1 | demultiplexer_2_out1;  // OR_Gate or_1, 8 bits wide
  assign \Ядро_1  = demultiplexer_1_out0 | demultiplexer_2_out0;  // OR_Gate or_2, 8 bits wide
endmodule
