// Logisim project П-2МУ.circ as structural Verilog: 7 circuits, main circuit Top-Level
module main (
  output [31:0] \А ,
  output [31:0] \Д ,
  output [31:0] \Б ,
  output [31:0] \Е ,
  output [3:0] \прер ,
  output [31:0] \В ,
  output [31:0] \Ё ,
  output [31:0] \Г ,
  output [31:0] \Ж ,
  output [31:0] \З 
);

  wire button_1_out, clock_1_out, comparator_1_eq, cu_1_jmp, cu_1_jmp_2, cu_1_rc, cu_1_rm, cu_1_rw, cu_1_wm,
       demultiplexer_2_out0, demultiplexer_2_out1, multiplexer_5_out, not_1_out, or_1_out;
  wire [3:0] cu_1_alu;
  wire [15:0] bit_extender_1_out, counter_1_q, multiplexer_1_out, multiplexer_2_out, multiplexer_3_out,
       multiplexer_4_out, register_1_q;
  wire [31:0] \alu_1_выход , demultiplexer_1_out0, demultiplexer_1_out1, multiplexer_6_out, ram_1_data,
       \reg_1_выход_1 , \reg_1_выход_2 , register_2_q;
  wire [31:16] register_1_q_2;

  Clock clock_1 (.out(clock_1_out));
  Multiplexer #(.width(16)) multiplexer_1 (
    .in0(16'h1), .in1(multiplexer_3_out), .out(multiplexer_1_out), .sel(cu_1_jmp_2));  // open: en
  Counter #(.width(16), .max('hffff)) counter_1 (
    .D(multiplexer_1_out), .Q(counter_1_q), .clk(demultiplexer_2_out0), .clr(button_1_out));  // open: load, count, carry
  Button button_1 (.out(button_1_out));
  Multiplexer #(.width(16)) multiplexer_2 (
    .in0(counter_1_q), .in1(register_1_q), .out(multiplexer_2_out), .sel(cu_1_rm));  // open: en
  Multiplexer #(.width(16)) multiplexer_3 (
    .in0(bit_extender_1_out), .in1(multiplexer_4_out), .out(multiplexer_3_out), .sel(cu_1_jmp));  // open: en
  not not_1 (not_1_out, cu_1_wm);
  RAM #(.addrWidth(16), .dataWidth(32), .bus("separate")) ram_1 (
    .addr(multiplexer_2_out), .din(\Ж ), .data(ram_1_data), .str(cu_1_wm), .ld(not_1_out));  // open: sel, clk, clr
  Multiplexer #(.width(16)) multiplexer_4 (
    .in0(16'h1), .in1(bit_extender_1_out), .out(multiplexer_4_out), .sel(comparator_1_eq));  // open: en
  Demultiplexer #(.width(32)) demultiplexer_1 (
    .out0(demultiplexer_1_out0), .out1(demultiplexer_1_out1), .in(ram_1_data), .sel(cu_1_rm));  // open: en
  Demultiplexer demultiplexer_2 (
    .out0(demultiplexer_2_out0), .out1(demultiplexer_2_out1), .in(clock_1_out), .sel(cu_1_rm));  // open: en
  Register #(.width(32), .trigger("falling")) register_1 (
    .D(demultiplexer_1_out0), .Q({register_1_q_2, register_1_q}), .clk(clock_1_out));  // open: en, clr
  Bit_Extender #(.in_width(32)) bit_extender_1 (.in(\З ), .out(bit_extender_1_out));
  CU cu_1 (
    .\Такт (clock_1_out), .RW(cu_1_rw), .RC(cu_1_rc), .ALU(cu_1_alu), .JMP_2(cu_1_jmp_2), .JMP(cu_1_jmp),
    .INT(\прер ), .in_1(register_1_q_2), .RM(cu_1_rm), .WM(cu_1_wm));
  Register #(.width(32), .trigger("falling")) register_2 (
    .D(demultiplexer_1_out1), .Q(register_2_q), .clk(demultiplexer_2_out1));  // open: en, clr
  or or_1 (or_1_out, cu_1_rc, cu_1_rw);
  Multiplexer multiplexer_5 (.in0(1'b0), .in1(clock_1_out), .out(multiplexer_5_out), .sel(or_1_out));  // open: en
  Multiplexer #(.width(32)) multiplexer_6 (
    .in0(register_2_q), .in1(\alu_1_выход ), .out(multiplexer_6_out), .sel(cu_1_rc));  // open: en
  Comparator #(.width(32)) comparator_1 (
    .a(\reg_1_выход_1 ), .b(\reg_1_выход_2 ), .eq(comparator_1_eq));  // open: gt, lt
  Reg reg_1 (
    .\Вход_1 (register_1_q[7:0]), .\Вход_2 (register_1_q[15:8]), .\Запись (multiplexer_5_out),
    .\Выход_1 (\reg_1_выход_1 ), .\Выход_2 (\reg_1_выход_2 ), .\а (\А ), .\д (\Д ), .\б (\Б ), .\е (\Е ),
    .\в (\В ), .\ё (\Ё ), .\г (\Г ), .\ж (\Ж ), .\з (\З ), .\Данные (multiplexer_6_out));
  ALU alu_1 (
    .\Настройка (cu_1_alu), .\Такт (clock_1_out), .\Вход_1 (\reg_1_выход_1 ), .\Вход_2 (\reg_1_выход_2 ),
    .\Выход (\alu_1_выход ));
endmodule

module CU (
  input  [15:0] in_1,
  input  \Такт ,
  output JMP,
  output RW,
  output JMP_2,
  output RC,
  output [3:0] ALU,
  output RM,
  output WM,
  output [3:0] INT
);

  wire demultiplexer_1_out7, demultiplexer_1_out31, multiplexer_1_out;
  wire [4:0] bit_extender_1_out;

  Bit_Extender #(.in_width(16), .out_width(5)) bit_extender_1 (.in(in_1), .out(bit_extender_1_out));
  Multiplexer multiplexer_1 (.in0(1'b0), .in1(1'b1), .out(multiplexer_1_out), .sel(\Такт ));  // open: en
  Demultiplexer #(.select(5)) demultiplexer_1 (
    .out1(RW), .out2(RC), .out3(JMP_2), .out4(JMP), .out5(RM), .out6(WM), .out7(demultiplexer_1_out7),
    .out31(demultiplexer_1_out31), .in(multiplexer_1_out), .sel(bit_extender_1_out));  // open: out0, out8, out9, out10, out11, out12, out13, out14, out15, out16, out17, out18, out19, out20, out21, out22, out23, out24, out25, out26, out27, out28, out29, out30, en
  Multiplexer #(.width(4)) multiplexer_2 (
    .in0(4'b0000), .in1(in_1[8:5]), .out(ALU), .sel(demultiplexer_1_out7));  // open: en
  Multiplexer #(.width(4)) multiplexer_3 (
    .in0(4'b0000), .in1(in_1[8:5]), .out(INT), .sel(demultiplexer_1_out31));  // open: en
endmodule

module Reg (
  input  [7:0] \Вход_1 ,
  input  [7:0] \Вход_2 ,
  input  \Запись ,
  input  [31:0] \Данные ,
  output [31:0] \Выход_1 ,
  output [31:0] \Выход_2 ,
  output [31:0] \а ,
  output [31:0] \д ,
  output [31:0] \б ,
  output [31:0] \е ,
  output [31:0] \в ,
  output [31:0] \ё ,
  output [31:0] \г ,
  output [31:0] \ж ,
  output [31:0] \з 
);

  wire demultiplexer_2_out0, demultiplexer_2_out1, demultiplexer_2_out2, demultiplexer_2_out3,
       demultiplexer_2_out4, demultiplexer_2_out5, demultiplexer_2_out6, demultiplexer_2_out7,
       demultiplexer_2_out8;
  wire [3:0] bit_extender_1_out, bit_extender_2_out;
  wire [31:0] demultiplexer_1_out0, demultiplexer_1_out1, demultiplexer_1_out2, demultiplexer_1_out3,
       demultiplexer_1_out4, demultiplexer_1_out5, demultiplexer_1_out6, demultiplexer_1_out7,
       demultiplexer_1_out8;

  Bit_Extender #(.out_width(4)) bit_extender_1 (.in(\Вход_1 ), .out(bit_extender_1_out));
  Bit_Extender #(.out_width(4)) bit_extender_2 (.in(\Вход_2 ), .out(bit_extender_2_out));
  Register #(.width(32), .trigger("falling")) register_1 (
    .D(demultiplexer_1_out0), .Q(\а ), .clk(demultiplexer_2_out0));  // open: en, clr
  Multiplexer #(.select(4), .width(32)) multiplexer_1 (
    .in0(\а ), .in1(\б ), .in2(\в ), .in3(\г ), .in4(\д ), .in5(\е ), .in6(\ё ), .in7(\ж ), .in8(\з ),
    .out(\Выход_1 ), .sel(bit_extender_1_out));  // open: in9, in10, in11, in12, in13, in14, in15, en
  Register #(.width(32), .trigger("falling")) register_2 (
    .D(demultiplexer_1_out1), .Q(\б ), .clk(demultiplexer_2_out1));  // open: en, clr
  Demultiplexer #(.select(4), .width(32)) demultiplexer_1 (
    .out0(demultiplexer_1_out0), .out1(demultiplexer_1_out1), .out2(demultiplexer_1_out2),
    .out3(demultiplexer_1_out3), .out4(demultiplexer_1_out4), .out5(demultiplexer_1_out5),
    .out6(demultiplexer_1_out6), .out7(demultiplexer_1_out7), .out8(demultiplexer_1_out8), .in(\Данные ),
    .sel(bit_extender_1_out));  // open: out9, out10, out11, out12, out13, out14, out15, en
  Register #(.width(32), .trigger("falling")) register_3 (
    .D(demultiplexer_1_out2), .Q(\в ), .clk(demultiplexer_2_out2));  // open: en, clr
  Register #(.width(32), .trigger("falling")) register_4 (
    .D(demultiplexer_1_out3), .Q(\г ), .clk(demultiplexer_2_out3));  // open: en, clr
  Register #(.width(32), .trigger("falling")) register_5 (
    .D(demultiplexer_1_out4), .Q(\д ), .clk(demultiplexer_2_out4));  // open: en, clr
  Register #(.width(32), .trigger("falling")) register_6 (
    .D(demultiplexer_1_out5), .Q(\е ), .clk(demultiplexer_2_out5));  // open: en, clr
  Register #(.width(32), .trigger("falling")) register_7 (
    .D(demultiplexer_1_out6), .Q(\ё ), .clk(demultiplexer_2_out6));  // open: en, clr
  Demultiplexer #(.select(4)) demultiplexer_2 (
    .out0(demultiplexer_2_out0), .out1(demultiplexer_2_out1), .out2(demultiplexer_2_out2),
    .out3(demultiplexer_2_out3), .out4(demultiplexer_2_out4), .out5(demultiplexer_2_out5),
    .out6(demultiplexer_2_out6), .out7(demultiplexer_2_out7), .out8(demultiplexer_2_out8), .in(\Запись ),
    .sel(bit_extender_1_out));  // open: out9, out10, out11, out12, out13, out14, out15, en
  Multiplexer #(.select(4), .width(32)) multiplexer_2 (
    .in0(\а ), .in1(\б ), .in2(\в ), .in3(\г ), .in4(\д ), .in5(\е ), .in6(\ё ), .in7(\ж ), .in8(\з ),
    .out(\Выход_2 ), .sel(bit_extender_2_out));  // open: in9, in10, in11, in12, in13, in14, in15, en
  Register #(.width(32), .trigger("falling")) register_8 (
    .D(demultiplexer_1_out7), .Q(\ж ), .clk(demultiplexer_2_out7));  // open: en, clr
  Register #(.width(32), .trigger("falling")) register_9 (
    .D(demultiplexer_1_out8), .Q(\з ), .clk(demultiplexer_2_out8));  // open: en, clr
endmodule

module ALU (
  input  [3:0] \Настройка ,
  input  \Такт ,
  input  [31:0] \Вход_1 ,
  input  [31:0] \Вход_2 ,
  output [31:0] \Выход 
);

  wire adder_1_cout, comparator_1_eq, comparator_1_gt, comparator_1_lt, comparator_2_eq, subtractor_1_bout;
  wire [31:0] adder_1_out, and_1_out, bit_extender_1_out, bit_extender_2_out, bit_extender_3_out,
       bit_extender_4_out, bit_extender_5_out, bit_extender_6_out, divider_1_out, divider_1_rem,
       divider_2_rem, multiplexer_1_out, multiplier_1_cout, multiplier_1_out, negator_1_out, or_1_out,
       subtractor_1_out, xor_1_out;

  Adder #(.width(32)) adder_1 (.a(\Вход_1 ), .b(\Вход_2 ), .out(adder_1_out), .cout(adder_1_cout));  // open: cin
  Subtractor #(.width(32)) subtractor_1 (
    .a(\Вход_1 ), .b(\Вход_2 ), .out(subtractor_1_out), .bout(subtractor_1_bout));  // open: bin
  assign bit_extender_1_out = {{31{1'b1}}, subtractor_1_bout};  // Bit_Extender bit_extender_1
  Multiplier #(.width(32)) multiplier_1 (
    .a(\Вход_1 ), .b(\Вход_2 ), .out(multiplier_1_out), .cout(multiplier_1_cout));  // open: cin
  Divider #(.width(32)) divider_1 (
    .a(\Вход_1 ), .b(\Вход_2 ), .out(divider_1_out), .rem(divider_1_rem));  // open: upper
  Negator #(.width(32)) negator_1 (.in(\Вход_1 ), .out(negator_1_out));
  Comparator #(.width(32)) comparator_1 (
    .a(\Вход_1 ), .b(\Вход_2 ), .gt(comparator_1_gt), .eq(comparator_1_eq), .lt(comparator_1_lt));
  Divider #(.width(32)) divider_2 (.a(\Вход_1 ), .b(32'h2), .rem(divider_2_rem));  // open: out, upper
  assign bit_extender_2_out = {{31{1'b1}}, adder_1_cout};  // Bit_Extender bit_extender_2
  assign bit_extender_3_out = {{31{1'b1}}, comparator_1_gt};  // Bit_Extender bit_extender_3
  assign bit_extender_4_out = {{31{1'b1}}, comparator_1_eq};  // Bit_Extender bit_extender_4
  assign bit_extender_5_out = {{31{1'b1}}, comparator_1_lt};  // Bit_Extender bit_extender_5
  assign bit_extender_6_out = {{31{1'b1}}, comparator_2_eq};  // Bit_Extender bit_extender_6
  Comparator #(.width(32)) comparator_2 (.a(divider_2_rem), .b({32{1'b0}}), .eq(comparator_2_eq));  // open: gt, lt
  assign and_1_out = \Вход_1  & \Вход_2 ;  // AND_Gate and_1, 32 bits wide
  assign or_1_out = \Вход_1  | \Вход_2 ;  // OR_Gate or_1, 32 bits wide
  assign xor_1_out = \Вход_1  ^ \Вход_2 ;  // XOR_Gate xor_1, 32 bits wide
  Multiplexer #(.select(4), .width(32)) multiplexer_1 (
    .in0(adder_1_out), .in1(bit_extender_2_out), .in2(subtractor_1_out), .in3(bit_extender_1_out),
    .in4(multiplier_1_out), .in5(multiplier_1_cout), .in6(divider_1_out), .in7(divider_1_rem),
    .in8(negator_1_out), .in9(bit_extender_3_out), .in10(bit_extender_4_out), .in11(bit_extender_5_out),
    .in12(bit_extender_6_out), .in13(and_1_out), .in14(or_1_out), .in15(xor_1_out), .out(multiplexer_1_out),
    .sel(\Настройка ));  // open: en
  Register #(.width(32), .trigger("falling")) register_1 (
    .D(multiplexer_1_out), .Q(\Выход ), .clk(\Такт ));  // open: en, clr
endmodule

module Top_Level (
);

  wire clock_1_out, \commm_1_запись , \commm_1_обновление , \commm_1_сброс , \vcard_1_очистка ;
  wire [3:0] \main_1_прер ;
  wire [6:0] \vcard_1_видео_выход ;
  wire [31:0] \main_1_а , \main_1_д ;

  Clock clock_1 (.out(clock_1_out));
  CommM commm_1 (
    .\Команда (\main_1_прер ), .\Запись (\commm_1_запись ), .\Сброс (\commm_1_сброс ),
    .\Обновление (\commm_1_обновление ));
  main main_1 (.\А (\main_1_а ), .\Д (\main_1_д ), .\прер (\main_1_прер ));  // open: Б, Е, В, Ё, Г, Ж, З
  VCard vcard_1 (
    .\Адрес (\main_1_а ), .\Данные (\main_1_д ), .\такт (clock_1_out), .\Отчистка_экрана (\commm_1_сброс ),
    .\Обновление (\commm_1_обновление ), .\Запись (\commm_1_запись ), .\Видео_выход (\vcard_1_видео_выход ),
    .\Очистка (\vcard_1_очистка ));
  TTY tty_1 (.data(\vcard_1_видео_выход ), .clk(clock_1_out), .clr(\vcard_1_очистка ));  // open: we
endmodule

module VCard (
  input  [31:0] \Адрес ,
  input  [31:0] \Данные ,
  input  \такт ,
  input  \Отчистка_экрана ,
  input  \Обновление ,
  input  \Запись ,
  output [6:0] \Видео_выход ,
  output \Очистка 
);

  wire not_1_out;
  wire [23:0] bit_extender_1_out, counter_1_q, multiplexer_1_out;

  Bit_Extender #(.in_width(32), .out_width(24)) bit_extender_1 (.in(\Адрес ), .out(bit_extender_1_out));
  Counter #(.width(24), .max('hffffff)) counter_1 (
    .Q(counter_1_q), .clk(\такт ), .clr(\Отчистка_экрана ));  // open: load, D, count, carry
  Multiplexer #(.width(24)) multiplexer_1 (
    .in0(counter_1_q), .in1(bit_extender_1_out), .out(multiplexer_1_out), .sel(not_1_out));  // open: en
  RAM #(.addrWidth(24), .dataWidth(32)) ram_1 (
    .addr(multiplexer_1_out), .data(\Данные ), .clk(\такт ), .ld(not_1_out), .clr(\Отчистка_экрана ));  // open: sel
  not not_1 (not_1_out, \Запись );
  Bit_Extender #(.in_width(32), .out_width(7)) bit_extender_2 (.in(\Данные ), .out(\Видео_выход ));

  assign \Очистка  = \Отчистка_экрана ;
endmodule

module CommM (
  input  [3:0] \Команда ,
  output \Запись ,
  output \Сброс ,
  output \Обновление 
);

  Demultiplexer #(.select(4)) demultiplexer_1 (
    .out1(\Запись ), .out2(\Сброс ), .out3(\Обновление ), .in(1'b1), .sel(\Команда ));  // open: out0, out4, out5, out6, out7, out8, out9, out10, out11, out12, out13, out14, out15, en
endmodule
