// Logisim project П-3У.circ as structural Verilog: 5 circuits, main circuit main
module main (
  input  in_1
);

  wire and_1_out, clock_1_out, comparator_1_eq, counter_2_q, \cu_1_алу , \cu_1_алу_в_регистр , \cu_1_вывод ,
       \cu_1_жфепрыжок_если , \cu_1_загрузка_из_стека , \cu_1_запись_в_память , \cu_1_запись_в_регистр ,
       \cu_1_запись_в_стек , \cu_1_прыжок , \cu_1_регистр_в_регистр , \cu_1_смена_озу_память ,
       \cu_1_чтение_памяти , demultiplexer_3_out1, multiplexer_2_out, multiplexer_4_out, multiplexer_11_out,
       not_1_out, or_1_out, or_2_out, or_3_out, or_4_out, or_5_out;
  wire [4:0] cu_1_out_2;
  wire [15:0] adder_1_out, counter_1_q, demultiplexer_1_out0, demultiplexer_1_out1, demultiplexer_4_out1,
       multiplexer_1_out, multiplexer_3_out, multiplexer_6_out, multiplexer_7_out, undriven;
  wire [31:0] \alu_1_выход , demultiplexer_2_out0, demultiplexer_2_out1, multiplexer_5_out,
       multiplexer_8_out, multiplexer_9_out, multiplexer_10_out, ram_1_data, register_1_q, register_2_q,
       \regs_1_в2 , rom_1_data, \stack_1_выход , \Временный_Хегистр_Хранения_Данных_q ;
  wire [31:16] \regs_1_в1 ;

  Clock clock_1 (.out(clock_1_out));
  Adder #(.width(16)) adder_1 (.a(counter_1_q), .b(16'h1), .out(adder_1_out));  // open: cin, cout
  Multiplexer #(.width(16)) multiplexer_1 (
    .in0(adder_1_out), .in1(multiplexer_6_out), .out(multiplexer_1_out), .sel(or_1_out));  // open: en
  Multiplexer multiplexer_2 (.in0(clock_1_out), .out(multiplexer_2_out), .sel(or_2_out));  // open: in1, en
  Hex_Digit_Display hex_digit_display_1 (.value(register_2_q[31:28]));  // open: dp
  Hex_Digit_Display hex_digit_display_2 (.value(register_2_q[27:24]));  // open: dp
  Counter #(.width(16), .max('hffff)) counter_1 (
    .D(multiplexer_1_out), .Q(counter_1_q), .clk(multiplexer_2_out), .clr(in_1));  // open: load, count, carry
  Hex_Digit_Display hex_digit_display_3 (.value(register_2_q[23:20]));  // open: dp
  or or_1 (or_1_out, \cu_1_прыжок , \cu_1_регистр_в_регистр );
  Multiplexer #(.width(16)) multiplexer_3 (
    .in0(counter_1_q), .in1(undriven), .out(multiplexer_3_out), .sel(or_2_out));  // open: en
  Hex_Digit_Display hex_digit_display_4 (.value(register_2_q[19:16]));  // open: dp
  Hex_Digit_Display hex_digit_display_5 (.value(register_2_q[15:12]));  // open: dp
  Counter #(.width(1), .max('h1)) counter_2 (
    .D(\cu_1_смена_озу_память ), .Q(counter_2_q));  // open: load, count, carry, clk, clr
  Demultiplexer #(.width(16)) demultiplexer_1 (
    .out0(demultiplexer_1_out0), .out1(demultiplexer_1_out1), .in(multiplexer_3_out), .sel(counter_2_q));  // open: en
  Hex_Digit_Display hex_digit_display_6 (.value(register_2_q[11:8]));  // open: dp
  or or_2 (or_2_out, \cu_1_запись_в_память , \cu_1_чтение_памяти );
  Multiplexer multiplexer_4 (
    .in0(1'b0), .in1(\cu_1_запись_в_память ), .out(multiplexer_4_out), .sel(\cu_1_запись_в_память ));  // open: en
  Hex_Digit_Display hex_digit_display_7 (.value(register_2_q[3:0]));  // open: dp
  Hex_Digit_Display hex_digit_display_8 (.value(register_2_q[7:4]));  // open: dp
  not not_1 (not_1_out, multiplexer_4_out);
  cu cu_1 (
    .in_1(register_1_q[31:16]), .out_2(cu_1_out_2), .\Запись_в_Регистр (\cu_1_запись_в_регистр ),
    .\Чтение_Памяти (\cu_1_чтение_памяти ), .\Запись_в_память (\cu_1_запись_в_память ), .\АЛУ (\cu_1_алу ),
    .\Прыжок (\cu_1_прыжок ), .\жфеПрыжок_если (\cu_1_жфепрыжок_если ),
    .\Алу_в_регистр (\cu_1_алу_в_регистр ), .\регистр_в_регистр (\cu_1_регистр_в_регистр ),
    .\Смена_озу_память (\cu_1_смена_озу_память ), .\Запись_в_стек (\cu_1_запись_в_стек ),
    .\Загрузка_из_стека (\cu_1_загрузка_из_стека ), .\Вывод (\cu_1_вывод ));
  ROM #(.addrWidth(16), .dataWidth(32)) rom_1 (.addr(demultiplexer_1_out0), .data(rom_1_data));  // open: sel
  RAM #(.addrWidth(16), .dataWidth(32), .bus("separate")) ram_1 (
    .addr(demultiplexer_1_out1), .din(\regs_1_в2 ), .data(ram_1_data), .str(multiplexer_4_out),
    .clk(clock_1_out), .ld(not_1_out));  // open: sel, clr
  Multiplexer #(.width(32)) multiplexer_5 (
    .in0(rom_1_data), .in1(ram_1_data), .out(multiplexer_5_out), .sel(counter_2_q));  // open: en
  Demultiplexer #(.width(32)) demultiplexer_2 (
    .out0(demultiplexer_2_out0), .out1(demultiplexer_2_out1), .in(multiplexer_5_out),
    .sel(\cu_1_чтение_памяти ));  // open: en
  Demultiplexer demultiplexer_3 (
    .out1(demultiplexer_3_out1), .in(clock_1_out), .sel(\cu_1_чтение_памяти ));  // open: out0, en
  Multiplexer #(.width(16)) multiplexer_6 (
    .in0(demultiplexer_4_out1), .in1(multiplexer_7_out), .out(multiplexer_6_out), .sel(\cu_1_жфепрыжок_если ));  // open: en
  Register #(.width(32)) register_1 (.D(demultiplexer_2_out0), .Q(register_1_q), .clk(clock_1_out));  // open: en, clr
  Demultiplexer #(.width(16)) demultiplexer_4 (
    .out0(register_1_q[15:0]), .out1(demultiplexer_4_out1), .in(undriven), .sel(multiplexer_4_out));  // open: en
  Multiplexer #(.width(16)) multiplexer_7 (
    .in0(adder_1_out), .in1(demultiplexer_4_out1), .out(multiplexer_7_out), .sel(and_1_out));  // open: en
  Register #(.width(32), .trigger("falling")) \u_Временный_Хегистр_Хранения_Данных  (
    .D(demultiplexer_2_out1), .Q(\Временный_Хегистр_Хранения_Данных_q ), .clk(demultiplexer_3_out1));  // open: en, clr
  or or_3 (or_3_out, \cu_1_алу_в_регистр , \cu_1_регистр_в_регистр , \cu_1_загрузка_из_стека );
  Multiplexer #(.width(32)) multiplexer_8 (
    .in0(\Временный_Хегистр_Хранения_Данных_q ), .in1(multiplexer_9_out), .out(multiplexer_8_out),
    .sel(or_3_out));  // open: en
  stack stack_1 (
    .\Значение_входа ({\regs_1_в1 , demultiplexer_4_out1}), .\запись (\cu_1_запись_в_стек ),
    .\такт (clock_1_out), .\чтение (\cu_1_загрузка_из_стека ), .\Выход (\stack_1_выход ));
  or or_4 (or_4_out, \cu_1_запись_в_регистр , \cu_1_регистр_в_регистр , \cu_1_алу_в_регистр );
  Multiplexer #(.width(32)) multiplexer_9 (
    .in0(\alu_1_выход ), .in1(multiplexer_10_out), .out(multiplexer_9_out), .sel(or_5_out));  // open: en
  regs regs_1 (
    .\А1 (register_1_q[7:0]), .\А2 (register_1_q[15:8]), .\Д1 (multiplexer_8_out), .\такт (clock_1_out),
    .\Запись (or_4_out), .\В1 ({\regs_1_в1 , demultiplexer_4_out1}), .\В2 (\regs_1_в2 ));
  Multiplexer #(.width(32)) multiplexer_10 (
    .in0(\regs_1_в2 ), .in1(\stack_1_выход ), .out(multiplexer_10_out), .sel(\cu_1_загрузка_из_стека ));  // open: en
  Multiplexer multiplexer_11 (.in0(1'b0), .in1(clock_1_out), .out(multiplexer_11_out), .sel(\cu_1_вывод ));  // open: en
  or or_5 (or_5_out, \cu_1_регистр_в_регистр , \cu_1_загрузка_из_стека );
  and and_1 (and_1_out, comparator_1_eq, \cu_1_жфепрыжок_если );
  Register #(.width(32), .trigger("falling")) register_2 (
    .D({\regs_1_в1 , demultiplexer_4_out1}), .Q(register_2_q), .clk(multiplexer_11_out));  // open: en, clr
  Comparator #(.width(32)) comparator_1 (.a(\regs_1_в2 ), .b({32{1'b1}}), .eq(comparator_1_eq));  // open: gt, lt
  ALU alu_1 (
    .\Команда (cu_1_out_2), .\такт (clock_1_out), .\Запись (\cu_1_алу ),
    .\В1 ({\regs_1_в1 , demultiplexer_4_out1}), .\В2 (\regs_1_в2 ), .\Выход (\alu_1_выход ));
endmodule

module regs (
  input  [7:0] \А1 ,
  input  [7:0] \А2 ,
  input  [31:0] \Д1 ,
  input  \такт ,
  input  \Запись ,
  output [31:0] \В1 ,
  output [31:0] \В2 
);

  wire demultiplexer_2_out0, demultiplexer_2_out1, demultiplexer_2_out2, demultiplexer_2_out3,
       demultiplexer_2_out4, demultiplexer_2_out5, demultiplexer_2_out6, demultiplexer_2_out7,
       demultiplexer_2_out8, multiplexer_2_out;
  wire [3:0] bit_extender_1_out, bit_extender_2_out;
  wire [31:0] demultiplexer_1_out0, demultiplexer_1_out1, demultiplexer_1_out2, demultiplexer_1_out3,
       demultiplexer_1_out4, demultiplexer_1_out5, demultiplexer_1_out6, demultiplexer_1_out7,
       demultiplexer_1_out8, \А_q , \Б_q , \В_q , \Г_q , \Д_q , \Е_q , \Ж_q , \З_q , \Ё_q ;

  Bit_Extender #(.out_width(4)) bit_extender_1 (.in(\А1 ), .out(bit_extender_1_out));
  Bit_Extender #(.out_width(4)) bit_extender_2 (.in(\А2 ), .out(bit_extender_2_out));
  Multiplexer #(.select(4), .width(32)) multiplexer_1 (
    .in0(\А_q ), .in1(\Б_q ), .in2(\В_q ), .in3(\Г_q ), .in4(\Д_q ), .in5(\Е_q ), .in6(\Ё_q ), .in7(\Ж_q ),
    .in8(\З_q ), .out(\В1 ), .sel(bit_extender_1_out));  // open: in9, in10, in11, in12, in13, in14, in15, en
  Register #(.width(32), .trigger("falling")) \u_А  (
    .D(demultiplexer_1_out0), .Q(\А_q ), .clk(demultiplexer_2_out0));  // open: en, clr
  Demultiplexer #(.select(4), .width(32)) demultiplexer_1 (
    .out0(demultiplexer_1_out0), .out1(demultiplexer_1_out1), .out2(demultiplexer_1_out2),
    .out3(demultiplexer_1_out3), .out4(demultiplexer_1_out4), .out5(demultiplexer_1_out5),
    .out6(demultiplexer_1_out6), .out7(demultiplexer_1_out7), .out8(demultiplexer_1_out8), .in(\Д1 ),
    .sel(bit_extender_1_out));  // open: out9, out10, out11, out12, out13, out14, out15, en
  Multiplexer multiplexer_2 (.in0(1'b0), .in1(\такт ), .out(multiplexer_2_out), .sel(\Запись ));  // open: en
  Register #(.width(32), .trigger("falling")) \u_Б  (
    .D(demultiplexer_1_out1), .Q(\Б_q ), .clk(demultiplexer_2_out1));  // open: en, clr
  Register #(.width(32), .trigger("falling")) \u_Ё  (
    .D(demultiplexer_1_out6), .Q(\Ё_q ), .clk(demultiplexer_2_out6));  // open: en, clr
  Register #(.width(32), .trigger("falling")) \u_В  (
    .D(demultiplexer_1_out2), .Q(\В_q ), .clk(demultiplexer_2_out2));  // open: en, clr
  Register #(.width(32), .trigger("falling")) \u_Г  (
    .D(demultiplexer_1_out3), .Q(\Г_q ), .clk(demultiplexer_2_out3));  // open: en, clr
  Register #(.width(32), .trigger("falling")) \u_Ж  (
    .D(demultiplexer_1_out7), .Q(\Ж_q ), .clk(demultiplexer_2_out7));  // open: en, clr
  Register #(.width(32), .trigger("falling")) \u_З  (
    .D(demultiplexer_1_out8), .Q(\З_q ), .clk(demultiplexer_2_out8));  // open: en, clr
  Register #(.width(32), .trigger("falling")) \u_Д  (
    .D(demultiplexer_1_out4), .Q(\Д_q ), .clk(demultiplexer_2_out4));  // open: en, clr
  Demultiplexer #(.select(4)) demultiplexer_2 (
    .out0(demultiplexer_2_out0), .out1(demultiplexer_2_out1), .out2(demultiplexer_2_out2),
    .out3(demultiplexer_2_out3), .out4(demultiplexer_2_out4), .out5(demultiplexer_2_out5),
    .out6(demultiplexer_2_out6), .out7(demultiplexer_2_out7), .out8(demultiplexer_2_out8),
    .in(multiplexer_2_out), .sel(bit_extender_1_out));  // open: out9, out10, out11, out12, out13, out14, out15, en
  Multiplexer #(.select(4), .width(32)) multiplexer_3 (
    .in0(\А_q ), .in1(\Б_q ), .in2(\В_q ), .in3(\Г_q ), .in4(\Д_q ), .in5(\Е_q ), .in6(\Ё_q ), .in7(\Ж_q ),
    .in8(\З_q ), .out(\В2 ), .sel(bit_extender_2_out));  // open: in9, in10, in11, in12, in13, in14, in15, en
  Register #(.width(32), .trigger("falling")) \u_Е  (
    .D(demultiplexer_1_out5), .Q(\Е_q ), .clk(demultiplexer_2_out5));  // open: en, clr
endmodule

module cu (
  input  [15:0] in_1,
  output [4:0] out_2,
  output \Запись_в_Регистр ,
  output \Чтение_Памяти ,
  output \Запись_в_память ,
  output \АЛУ ,
  output \Прыжок ,
  output \жфеПрыжок_если ,
  output \Алу_в_регистр ,
  output \регистр_в_регистр ,
  output \Смена_озу_память ,
  output \Запись_в_стек ,
  output \Загрузка_из_стека ,
  output \Вывод 
);

  Decoder #(.select(5)) decoder_1 (
    .out1(\Запись_в_Регистр ), .out2(\Чтение_Памяти ), .out3(\Запись_в_память ), .out4(\АЛУ ),
    .out5(\Прыжок ), .out6(\жфеПрыжок_если ), .out7(\Алу_в_регистр ), .out8(\регистр_в_регистр ),
    .out9(\Смена_озу_память ), .out10(\Запись_в_стек ), .out11(\Загрузка_из_стека ), .out12(\Вывод ),
    .sel(in_1[4:0]));  // open: out0, out13, out14, out15, out16, out17, out18, out19, out20, out21, out22, out23, out24, out25, out26, out27, out28, out29, out30, out31, en

  assign out_2 = in_1[9:5];
endmodule

module ALU (
  input  [4:0] \Команда ,
  input  \такт ,
  input  \Запись ,
  input  [31:0] \В1 ,
  input  [31:0] \В2 ,
  output [31:0] \Выход 
);

  wire adder_1_cout, comparator_1_eq, comparator_1_gt, comparator_1_lt, multiplexer_1_out, subtractor_1_bout;
  wire [4:0] bit_extender_1_out;
  wire [31:0] adder_1_out, and_1_out, bit_extender_2_out, bit_extender_3_out, bit_extender_4_out,
       bit_extender_5_out, bit_extender_6_out, divider_1_out, divider_1_rem, even_parity_1_out,
       multiplexer_2_out, multiplier_1_cout, multiplier_1_out, negator_1_out, or_1_out, shifter_1_out,
       shifter_2_out, subtractor_1_out, xor_1_out;

  Bit_Extender #(.in_width(32), .out_width(5)) bit_extender_1 (.in(\В2 ), .out(bit_extender_1_out));
  Adder #(.width(32)) adder_1 (.a(\В1 ), .b(\В2 ), .out(adder_1_out), .cout(adder_1_cout));  // open: cin
  Subtractor #(.width(32)) subtractor_1 (
    .a(\В1 ), .b(\В2 ), .out(subtractor_1_out), .bout(subtractor_1_bout));  // open: bin
  Multiplier #(.width(32)) multiplier_1 (
    .a(\В1 ), .b(\В2 ), .out(multiplier_1_out), .cout(multiplier_1_cout));  // open: cin
  Divider #(.width(32)) divider_1 (.a(\В1 ), .b(\В2 ), .out(divider_1_out), .rem(divider_1_rem));  // open: upper
  Comparator #(.width(32)) comparator_1 (
    .a(\В1 ), .b(\В2 ), .gt(comparator_1_gt), .eq(comparator_1_eq), .lt(comparator_1_lt));
  Shifter #(.width(32)) shifter_1 (.in(\В1 ), .\dist (bit_extender_1_out), .out(shifter_1_out));
  Shifter #(.width(32), .shift("lr")) shifter_2 (.in(\В1 ), .\dist (bit_extender_1_out), .out(shifter_2_out));
  assign and_1_out = \В1  & \В2 ;  // AND_Gate and_1, 32 bits wide
  assign or_1_out = \В1  | \В2 ;  // OR_Gate or_1, 32 bits wide
  assign xor_1_out = \В1  ^ \В2 ;  // XOR_Gate xor_1, 32 bits wide
  assign even_parity_1_out = ~(\В1  ^ \В2 );  // Even_Parity even_parity_1, 32 bits wide
  Negator #(.width(32)) negator_1 (.in(\В1 ), .out(negator_1_out));
  assign bit_extender_2_out = {{31{1'b1}}, adder_1_cout};  // Bit_Extender bit_extender_2
  assign bit_extender_3_out = {{31{1'b1}}, subtractor_1_bout};  // Bit_Extender bit_extender_3
  assign bit_extender_4_out = {{31{1'b1}}, comparator_1_gt};  // Bit_Extender bit_extender_4
  assign bit_extender_5_out = {{31{1'b1}}, comparator_1_eq};  // Bit_Extender bit_extender_5
  assign bit_extender_6_out = {{31{1'b1}}, comparator_1_lt};  // Bit_Extender bit_extender_6
  Multiplexer multiplexer_1 (.in0(1'b0), .in1(\такт ), .out(multiplexer_1_out), .sel(\Запись ));  // open: en
  Multiplexer #(.select(5), .width(32)) multiplexer_2 (
    .in0(adder_1_out), .in1(bit_extender_2_out), .in2(subtractor_1_out), .in3(bit_extender_3_out),
    .in4(multiplier_1_out), .in5(multiplier_1_cout), .in6(divider_1_out), .in7(divider_1_rem),
    .in8(bit_extender_4_out), .in9(bit_extender_5_out), .in10(bit_extender_6_out), .in11(shifter_1_out),
    .in12(shifter_2_out), .in13(and_1_out), .in14(or_1_out), .in15(xor_1_out), .in16(even_parity_1_out),
    .in17(negator_1_out), .out(multiplexer_2_out), .sel(\Команда ));  // open: in18, in19, in20, in21, in22, in23, in24, in25, in26, in27, in28, in29, in30, in31, en
  Register #(.width(32), .trigger("falling")) register_1 (
    .D(multiplexer_2_out), .Q(\Выход ), .clk(multiplexer_1_out));  // open: en, clr
endmodule

module stack (
  input  [31:0] \Значение_входа ,
  input  \запись ,
  input  \такт ,
  input  \чтение ,
  output [31:0] \Выход 
);

  wire multiplexer_1_out, or_1_out;
  wire [7:0] adder_1_out, counter_1_q, multiplexer_2_out, subtractor_1_out;

  or or_1 (or_1_out, \чтение , \запись );
  Multiplexer multiplexer_1 (.in0(1'b0), .in1(\такт ), .out(multiplexer_1_out), .sel(or_1_out));  // open: en
  Adder adder_1 (.a(counter_1_q), .b(8'h1), .out(adder_1_out));  // open: cin, cout
  Subtractor subtractor_1 (.a(counter_1_q), .b(8'h1), .out(subtractor_1_out));  // open: bin, bout
  Multiplexer #(.width(8)) multiplexer_2 (
    .in0(adder_1_out), .in1(subtractor_1_out), .out(multiplexer_2_out), .sel(\чтение ));  // open: en
  Counter #(.ongoal("stay")) counter_1 (
    .load(\чтение ), .D(multiplexer_2_out), .Q(counter_1_q), .clk(multiplexer_1_out));  // open: count, carry, clr
  RAM #(.dataWidth(32), .bus("separate")) ram_1 (
    .addr(counter_1_q), .din(\Значение_входа ), .data(\Выход ), .clk(multiplexer_1_out));  // open: str, sel, ld, clr
endmodule
