// Logisim project P_4.circ as structural Verilog: 5 circuits, main circuit main
module main (
  input  in_1,
  input  in_2
);

  wire button_1_out, clock_1_out, cu_1_alu, cu_1_ar, cu_1_ot, cu_1_pop, cu_1_push, cu_1_rm, cu_1_wm, cu_1_wr,
       demultiplexer_2_out1, multiplexer_1_out, multiplexer_4_out, not_1_out;
  wire [3:0] register_1_q, register_1_q_2, register_1_q_3, register_1_q_4, register_1_q_5, register_1_q_6,
       register_1_q_7, register_1_q_8;
  wire [4:0] cu_1_out_2;
  wire [15:0] adder_1_out, counter_1_q, multiplexer_2_out, multiplexer_3_out, undriven, undriven_3;
  wire [31:0] alu_1_outa, demultiplexer_1_out0, demultiplexer_1_out1, multiplexer_5_out, multiplexer_6_out,
       ram_1_dout, register_2_q, register_3_q, stack_1_datao, undriven_2, undriven_4, undriven_5;

  Clock clock_1 (.out(clock_1_out));
  Button button_1 (.out(button_1_out));
  Hex_Digit_Display hex_digit_display_1 (.value(register_1_q_8));  // open: dp
  Adder #(.width(16)) adder_1 (.a(counter_1_q), .b(16'h1), .out(adder_1_out));  // open: cin, cout
  Multiplexer multiplexer_1 (.in0(clock_1_out), .out(multiplexer_1_out), .sel(cu_1_rm));  // open: in1
  Hex_Digit_Display hex_digit_display_2 (.value(register_1_q_7));  // open: dp
  Hex_Digit_Display hex_digit_display_3 (.value(register_1_q_6));  // open: dp
  Multiplexer #(.width(16)) multiplexer_2 (.in0(adder_1_out), .in1(undriven), .out(multiplexer_2_out), .sel(in_2));
  Counter #(.max('hffff), .width(16)) counter_1 (
    .D(multiplexer_2_out), .Q(counter_1_q), .clk(multiplexer_1_out), .clr(button_1_out));  // open: load, count, carry, up
  Hex_Digit_Display hex_digit_display_4 (.value(register_1_q_5));  // open: dp
  not not_1 (not_1_out, in_1);
  RAM #(.addrWidth(16), .dataWidth(32), .\type ("nonvolatile")) ram_1 (
    .addr(multiplexer_3_out), .we(in_1), .oe(not_1_out), .clk(clock_1_out), .din(undriven_2),
    .dout(ram_1_dout));
  Multiplexer #(.width(16)) multiplexer_3 (.in0(counter_1_q), .in1(undriven_3), .out(multiplexer_3_out), .sel(cu_1_rm));
  Hex_Digit_Display hex_digit_display_5 (.value(register_1_q_4));  // open: dp
  Hex_Digit_Display hex_digit_display_6 (.value(register_1_q_3));  // open: dp
  Hex_Digit_Display hex_digit_display_7 (.value(register_1_q_2));  // open: dp
  Hex_Digit_Display hex_digit_display_8 (.value(register_1_q));  // open: dp
  Demultiplexer #(.width(32)) demultiplexer_1 (
    .out0(demultiplexer_1_out0), .out1(demultiplexer_1_out1), .in(ram_1_dout), .sel(cu_1_rm));
  Register #(.width(32)) register_1 (
    .D(undriven_4),
    .Q({register_1_q_8, register_1_q_7, register_1_q_6, register_1_q_5, register_1_q_4, register_1_q_3, register_1_q_2, register_1_q}),
    .clk(multiplexer_4_out));  // open: en, clr
  Register #(.width(32)) register_2 (.D(demultiplexer_1_out0), .Q(register_2_q), .clk(clock_1_out));  // open: en, clr
  Demultiplexer demultiplexer_2 (.out1(demultiplexer_2_out1), .in(clock_1_out), .sel(cu_1_rm));  // open: out0
  Multiplexer multiplexer_4 (.in0(1'b0), .in1(clock_1_out), .out(multiplexer_4_out), .sel(cu_1_ot));
  Register #(.width(32)) register_3 (
    .D(demultiplexer_1_out1), .Q(register_3_q), .clk(demultiplexer_2_out1));  // open: en, clr
  cu cu_1 (
    .in_1(register_2_q[31:16]), .out_2(cu_1_out_2), .WR(cu_1_wr), .RM(cu_1_rm), .WM(cu_1_wm), .ALU(cu_1_alu),
    .AR(cu_1_ar), .PUSH(cu_1_push), .POP(cu_1_pop), .OT(cu_1_ot));  // open: JMP, JIF, RtR
  Multiplexer #(.width(32)) multiplexer_5 (
    .in0(register_3_q), .in1(multiplexer_6_out), .out(multiplexer_5_out), .sel(cu_1_rm));
  Multiplexer #(.width(32)) multiplexer_6 (
    .in0(alu_1_outa), .in1(stack_1_datao), .out(multiplexer_6_out), .sel(cu_1_ar));
  Stack stack_1 (.DATA(undriven_4), .CLK(clock_1_out), .RD(cu_1_pop), .WR(cu_1_push), .DATAO(stack_1_datao));
  ALU alu_1 (
    .in_1(cu_1_out_2), .CLK(clock_1_out), .ALUON(cu_1_alu), .A1(undriven_4), .A2(undriven_5),
    .OUTA(alu_1_outa));
endmodule

module cu (
  input  [15:0] in_1,
  output [4:0] out_2,
  output WR,
  output RM,
  output WM,
  output ALU,
  output JMP,
  output JIF,
  output AR,
  output RtR,
  output PUSH,
  output POP,
  output OT
);

  Decoder #(.select(5)) decoder_1 (
    .out1(WR), .out2(RM), .out3(WM), .out4(ALU), .out5(JMP), .out6(JIF), .out7(AR), .out8(RtR), .out9(PUSH),
    .out10(POP), .out11(OT), .sel(in_1[4:0]));  // open: out0, out12, out13, out14, out15, out16, out17, out18, out19, out20, out21, out22, out23, out24, out25, out26, out27, out28, out29, out30, out31, en

  assign out_2 = in_1[9:5];
endmodule

module RegFile (
  input  [7:0] A1,
  input  [7:0] A2,
  input  [31:0] D1,
  input  CLK,
  input  WRT
);

  wire [3:0] bit_extender_1_out, bit_extender_2_out;

  Bit_Extender #(.out_width(4)) bit_extender_1 (.in(A1), .out(bit_extender_1_out));
  Bit_Extender #(.out_width(4)) bit_extender_2 (.in(A2), .out(bit_extender_2_out));
endmodule

module Stack (
  input  [31:0] DATA,
  input  CLK,
  input  RD,
  input  WR,
  output [31:0] DATAO
);

  wire button_1_out, not_1_out;
  wire [7:0] counter_1_q;
  wire [31:0] ram_1_dout;

  not not_1 (not_1_out, RD);
  Button button_1 (.out(button_1_out));
  Counter #(.ongoal("stay")) counter_1 (
    .Q(counter_1_q), .up(not_1_out), .clk(CLK), .clr(button_1_out));  // open: load, D, count, carry
  RAM #(.dataWidth(32)) ram_1 (.addr(counter_1_q), .we(WR), .oe(RD), .clk(CLK), .din(DATA), .dout(ram_1_dout));
  Multiplexer #(.width(32)) multiplexer_1 (.in0({32{1'b0}}), .in1(ram_1_dout), .out(DATAO), .sel(RD));
endmodule

module ALU (
  input  [4:0] in_1,
  input  CLK,
  input  ALUON,
  input  [31:0] A1,
  input  [31:0] A2,
  output [31:0] OUTA
);

  wire adder_1_cout, comparator_1_eq, comparator_1_gt, comparator_1_lt, inttofp_1_p2, inttofp_1_p3,
       inttofp_1_p4, inttofp_1_p5, multiplexer_1_out, subtractor_1_bout;
  wire [4:0] bit_extender_1_out;
  wire [31:0] adder_1_out, bit_extender_2_out, bit_extender_3_out, bit_extender_4_out, bit_extender_5_out,
       bit_extender_6_out, bit_extender_7_out, bit_extender_8_out, bit_extender_9_out, bit_extender_10_out,
       divider_1_out, divider_1_rem, fpadder_1_out, fpdivider_1_out, fpmultiplier_1_out, fpsubtractor_1_out,
       fptoint_1_p2, inttofp_1_p6, multiplexer_2_out, multiplier_1_cout, multiplier_1_out, negator_1_out,
       shifter_1_out, shifter_2_out, subtractor_1_out;

  Bit_Extender #(.in_width(32), .out_width(5)) bit_extender_1 (.in(A2), .out(bit_extender_1_out));
  Adder #(.width(32)) adder_1 (.a(A1), .b(A2), .out(adder_1_out), .cout(adder_1_cout));  // open: cin
  Subtractor #(.width(32)) subtractor_1 (
    .a(A1), .b(A2), .out(subtractor_1_out), .bout(subtractor_1_bout));  // open: bin
  Multiplier #(.mode("twosComplement"), .width(32)) multiplier_1 (
    .a(A1), .b(A2), .out(multiplier_1_out), .cout(multiplier_1_cout));  // open: cin
  Divider #(.mode("twosComplement"), .width(32)) divider_1 (
    .a(A1), .b(A2), .out(divider_1_out), .rem(divider_1_rem));  // open: upper
  Negator #(.width(32)) negator_1 (.in(A1), .out(negator_1_out));
  Comparator #(.width(32)) comparator_1 (
    .a(A1), .b(A2), .gt(comparator_1_gt), .eq(comparator_1_eq), .lt(comparator_1_lt));
  Shifter #(.width(32)) shifter_1 (.in(A1), .\dist (bit_extender_1_out), .out(shifter_1_out));
  Shifter #(.shift("lr"), .width(32)) shifter_2 (.in(A1), .\dist (bit_extender_1_out), .out(shifter_2_out));
  FPAdder fpadder_1 (.a(A1), .b(A2), .out(fpadder_1_out));
  FPSubtractor fpsubtractor_1 (.a(A1), .b(A2), .out(fpsubtractor_1_out));
  FPMultiplier fpmultiplier_1 (.a(A1), .b(A2), .out(fpmultiplier_1_out));
  FPDivider fpdivider_1 (.a(A1), .b(A2), .out(fpdivider_1_out));
  // IntToFP #(.width(32)) inttofp_1: pin names not known; wires that end beside it: A1, inttofp_1_p2, inttofp_1_p3, inttofp_1_p4, inttofp_1_p5, inttofp_1_p6
  // FPToInt #(.width(32)) fptoint_1: pin names not known; wires that end beside it: A1, fptoint_1_p2
  Multiplexer multiplexer_1 (.in0(1'b0), .in1(CLK), .out(multiplexer_1_out), .sel(ALUON));
  assign bit_extender_2_out = {{31{adder_1_cout}}, adder_1_cout};  // Bit_Extender bit_extender_2
  assign bit_extender_3_out = {{31{subtractor_1_bout}}, subtractor_1_bout};  // Bit_Extender bit_extender_3
  assign bit_extender_4_out = {{31{comparator_1_gt}}, comparator_1_gt};  // Bit_Extender bit_extender_4
  assign bit_extender_5_out = {{31{comparator_1_eq}}, comparator_1_eq};  // Bit_Extender bit_extender_5
  assign bit_extender_6_out = {{31{comparator_1_lt}}, comparator_1_lt};  // Bit_Extender bit_extender_6
  assign bit_extender_7_out = {{31{inttofp_1_p2}}, inttofp_1_p2};  // Bit_Extender bit_extender_7
  assign bit_extender_8_out = {{31{inttofp_1_p3}}, inttofp_1_p3};  // Bit_Extender bit_extender_8
  assign bit_extender_9_out = {{31{inttofp_1_p4}}, inttofp_1_p4};  // Bit_Extender bit_extender_9
  assign bit_extender_10_out = {{31{inttofp_1_p5}}, inttofp_1_p5};  // Bit_Extender bit_extender_10
  Multiplexer #(.select(5), .width(32)) multiplexer_2 (
    .in0(adder_1_out), .in1(bit_extender_2_out), .in2(subtractor_1_out), .in3(bit_extender_3_out),
    .in4(multiplier_1_out), .in5(multiplier_1_cout), .in6(divider_1_out), .in7(divider_1_rem),
    .in8(negator_1_out), .in9(bit_extender_4_out), .in10(bit_extender_5_out), .in11(bit_extender_6_out),
    .in12(shifter_1_out), .in13(shifter_2_out), .in14(fpadder_1_out), .in15(bit_extender_7_out),
    .in16(fpsubtractor_1_out), .in17(bit_extender_8_out), .in18(fpmultiplier_1_out),
    .in19(bit_extender_9_out), .in20(fpdivider_1_out), .in21(bit_extender_10_out), .in22(inttofp_1_p6),
    .in23(fptoint_1_p2), .out(multiplexer_2_out), .sel(in_1));  // open: in24, in25, in26, in27, in28, in29, in30, in31
  Register #(.trigger("falling"), .width(32)) register_1 (
    .D(multiplexer_2_out), .Q(OUTA), .clk(multiplexer_1_out));  // open: en, clr
endmodule
